# Fritzing sketch led-controller (saved by Fritzing 0.9.3b)
circuit board: 5cm x 4cm
breadboards: 1

parts:
  T1 = Basic FET N-Channel [package="TO220 [THT]"]
  U1 = V_REG_MIC2920 [part_number=3.3v package=sot223]
  R1 = Resistor [tolerance=±5% resistance=1k package=THT]
  LED1 = LED - 3mm [color="Red (633nm)" package="3 mm [THT]"]
  Q1 = WeMos D1 Mini

nets:
  N1: T1.gate, R1.Pin_0
  N2: T1.drain, LED1.cathode
  GND: T1.source, U1.GND, Q1.G
  12V: U1.IN, LED1.anode
  N3: U1.OUT, Q1.3V3
  N4: R1.Pin_1, Q1.D6
